# Fritzing sketch ESP32CAM PAGAR (saved by Fritzing 0.8.7b)

parts:
  ESP32_-_Back1 = ESP32 - CAM
  Bat1 = battery_holder_dual_18650 [part_number=TBH-18650-2A-P]
  M1 = fc-51 [package=THT]
  LED1 = LEDs [package=led10mm]
  J1 = Piezo Speaker

nets:
  N1: ESP32_-_Back1.GPIO2, M1.pin1
  N2: ESP32_-_Back1.GPIO14, LED1.A, J1.pin2
  N3: ESP32_-_Back1.GND#7, Bat1.+#0, M1.pin2, LED1.C
  N4: ESP32_-_Back1.5V, Bat1.+#1, Bat1.+#3, M1.pin3
  N5: ESP32_-_Back1.GND#16, J1.pin1

notes:
  ESP32 CAM
  SUPLAY
  LED
  BUZEER

custom parts:
  ESP32 - CAM: The ESP32-CAM has a very competitive small-size camera module that can operate independently as a minimum system with a footprint of only 27*40.5*4.5mm and a deep sleep current of up to 6mA.
  battery_holder_dual_18650: TBH-18650-2A-P dual 18650 battery holder.
