# Fritzing sketch PINTU DEPAN (saved by Fritzing 0.8.7b)

parts:
  BAT1 = BC9VPC [package=bc9vpc]
  Sensor1 = TTP223B Capacitive Touch Sensor Module
  J1 = Basic Servo
  Part1 = Arduino Uno (Rev3) - ICSP

nets:
  N1: BAT1.V+, Part1.GND
  VCC: BAT1.V-, Sensor1.VCC, Part1.VIN
  GND: Sensor1.GND, J1.gnd
  N2: Sensor1.SIG, Part1.D9_PWM
  N3: J1.pulse, Part1.D10_PWM/SS

notes:
  SUPLAY
  SERVO
  TOUCH
  SYSTEM 2
  PINTU DEPAN

custom parts:
  TTP223B Capacitive Touch Sensor Module: The TTP223B capacitive touch sensor module uses the TTP223B IC. The appropriate voltage is approximately 2 to 5.5 volts.
