# Fritzing sketch RUANG DALAM DAN PINTU DEPAN (saved by Fritzing 0.8.7b)

parts:
  J1 = Piezo Speaker
  M1 = fc-51 [package=THT]
  LED1 = LEDs [package=led10mm]
  WeMos_D1_Mini1 = WeMos D1 Mini
  M3 = fc-51 [package=THT]
  LED2 = LEDs [package=led10mm]
  BAT1 = BC9VPC [package=bc9vpc]

nets:
  N1: J1.pin1, LED1.C
  N2: J1.pin2, LED1.A, WeMos_D1_Mini1.D5
  N3: M1.pin1, WeMos_D1_Mini1.D6
  N4: M1.pin2, WeMos_D1_Mini1.G, M3.pin2, LED2.C, BAT1.V+
  N5: M1.pin3, WeMos_D1_Mini1.5V, M3.pin3, BAT1.V-
  N6: WeMos_D1_Mini1.D0, LED2.A
  N7: WeMos_D1_Mini1.D7, M3.pin1

notes:
  SUPLAY
  IR 1
  LED 1
  IR 2
  WEMOS
  LED 2
  SYSTEM 2
  PINTU DEPAN
  SYSTEM 3
  RUANG DALAM
